// Logisim project CPUMaster.circ as structural Verilog
module main (
  input  Run,
  input  in_2,
  output [63:0] out_3
);

  wire and_2_out, and_3_out, and_4_out, and_5_out, and_6_out, cc_1_sf, cc_1_zf, clock_1_out, memrwcntr_1_re,
       memrwcntr_1_we;
  wire [1:0] SF_q;
  wire [3:0] fetch_1_icode, fetch_1_ifun, fetch_1_ra, fetch_1_rb, iCode_q, iFun_q, rA_q, rB_q;
  wire [7:0] adder_1_out, and_1_p1, multiplexer_1_out;
  wire [11:0] adder_2_out, new_pc_1_pc_new, PC_q;
  wire [63:0] datamemory_1_valm, decode_1_vala, decode_1_valb, fetch_1_valc, valA_q, valB_q, valC_q, valE_q;

  Clock clock_1 (.out(clock_1_out));
  Multiplexer #(.width(8)) multiplexer_1 (.in0(adder_1_out), .in1({8{1'b0}}), .out(multiplexer_1_out), .sel(in_2));
  // AND_Gate and_1: pin names not known; wires that end beside it: and_1_p1[0], and_1_p1[2], and_1_p1[4], and_1_p1[5], and_1_p1[6], and_1_p1[7], and_1_p1[1], and_1_p1[3]
  Register register_1 (.D(multiplexer_1_out), .en(clock_1_out), .clk(clock_1_out), .Q(and_1_p1));  // open: clr
  Register #(.width(12)) PC (.D(new_pc_1_pc_new), .en(Run), .clk(clock_1_out), .Q(PC_q));  // open: clr
  Adder adder_1 (.a(8'h1), .b(and_1_p1), .out(adder_1_out));  // open: cin, cout
  LedBar #(.matrixcols(12)) PC_current (
    .led0(new_pc_1_pc_new[11]), .led1(new_pc_1_pc_new[10]), .led2(new_pc_1_pc_new[9]),
    .led3(new_pc_1_pc_new[8]), .led4(new_pc_1_pc_new[7]), .led5(new_pc_1_pc_new[6]),
    .led6(new_pc_1_pc_new[5]), .led7(new_pc_1_pc_new[4]), .led8(new_pc_1_pc_new[3]),
    .led9(new_pc_1_pc_new[2]), .led10(new_pc_1_pc_new[1]), .led11(new_pc_1_pc_new[0]));
  Adder #(.width(12)) adder_2 (.a(PC_q), .b(12'ha), .out(adder_2_out));  // open: cin, cout
  Fetch fetch_1 (
    .PC(PC_q), .clock(clock_1_out), .icode(fetch_1_icode), .ifun(fetch_1_ifun), .rA(fetch_1_ra),
    .rB(fetch_1_rb), .valC(fetch_1_valc));
  and and_2 (and_2_out, ~and_1_p1[0], and_1_p1[1], ~and_1_p1[2], and_1_p1[3], ~and_1_p1[4], ~and_1_p1[5], ~and_1_p1[6], ~and_1_p1[7]);  // AND_Gate
  Register #(.width(4)) iCode (.D(fetch_1_icode), .en(and_2_out), .clk(clock_1_out), .Q(iCode_q));  // open: clr
  Register #(.width(4)) iFun (.D(fetch_1_ifun), .en(and_2_out), .clk(clock_1_out), .Q(iFun_q));  // open: clr
  Register #(.width(4)) rA (.D(fetch_1_ra), .en(and_2_out), .clk(clock_1_out), .Q(rA_q));  // open: clr
  Register #(.width(4)) rB (.D(fetch_1_rb), .en(and_2_out), .clk(clock_1_out), .Q(rB_q));  // open: clr
  Register #(.width(64)) valC (.D(fetch_1_valc), .en(and_2_out), .clk(clock_1_out), .Q(valC_q));  // open: clr
  Register #(.width(64)) valA (.D(decode_1_vala), .en(and_3_out), .clk(clock_1_out), .Q(valA_q));  // open: clr
  Decode decode_1 (
    .clock_ctr(and_1_p1), .icode(iCode_q), .valE(valE_q), .valM(datamemory_1_valm), .rA(rA_q), .rB(rB_q),
    .Clk(clock_1_out), .valA(decode_1_vala), .valB(decode_1_valb));
  Register #(.width(64)) valB (.D(decode_1_valb), .en(and_3_out), .clk(clock_1_out), .Q(valB_q));  // open: clr
  and and_3 (and_3_out, and_1_p1[0], and_1_p1[1], ~and_1_p1[2], and_1_p1[3], ~and_1_p1[4], ~and_1_p1[5], ~and_1_p1[6], ~and_1_p1[7]);  // AND_Gate
  ALU alu_1 (.icode(iCode_q), .valC(valC_q), .valA(valA_q), .valB(valB_q), .ifun(iFun_q), .out_6(out_3), .valE(out_3));
  Register #(.width(64)) valE (.D(out_3), .en(and_4_out), .clk(clock_1_out), .Q(valE_q));  // open: clr
  and and_4 (and_4_out, ~and_1_p1[0], ~and_1_p1[1], and_1_p1[2], and_1_p1[3], ~and_1_p1[4], ~and_1_p1[5], ~and_1_p1[6], ~and_1_p1[7]);  // AND_Gate
  CC cc_1 (.valE(valE_q), .ZF(cc_1_zf), .SF(cc_1_sf));
  and and_5 (and_5_out, ~and_1_p1[0], and_1_p1[1], ~and_1_p1[2], and_1_p1[3], ~and_1_p1[4], ~and_1_p1[5], ~and_1_p1[6], ~and_1_p1[7]);  // AND_Gate
  Register #(.width(1)) ZF (.D(cc_1_zf), .en(and_6_out), .clk(clock_1_out), .Q(SF_q[1]));  // open: clr
  Register #(.width(1)) SF (.D(cc_1_sf), .en(and_6_out), .clk(clock_1_out), .Q(SF_q[0]));  // open: clr
  and and_6 (and_6_out, ~iCode_q[3], iCode_q[2], iCode_q[1], ~iCode_q[0], and_5_out);  // AND_Gate
  memRWCntr memrwcntr_1 (.icode(iCode_q), .clk_counter(and_1_p1), .WE(memrwcntr_1_we), .RE(memrwcntr_1_re));
  dataMemory datamemory_1 (
    .clock(clock_1_out), .WE(memrwcntr_1_we), .RE(memrwcntr_1_re), .valE(valE_q), .valA(valA_q),
    .valM(datamemory_1_valm));  // open: out_7
  New_PC new_pc_1 (
    .Val_P(adder_2_out), .Val_M(datamemory_1_valm), .Val_C(valC_q), .CC_flags(SF_q), .icode(fetch_1_icode),
    .ifun(fetch_1_ifun), .Reset(in_2), .PC_NEW(new_pc_1_pc_new));

  // Notes on the sheet:
  //   clock counter reset
  //   set timing diagram
  //   PC increment
  //   set timing diagram
  //   set timing diagram
  //   set timing diagram
  //   timing & icode = OP
  //   set timing diagram
  //   set timing
endmodule

module instructionMemory (
  input  [11:0] PC,
  input  clk,
  output [7:0] Byte0,
  output [7:0] Byte1,
  output [7:0] Byte2,
  output [7:0] Byte3,
  output [7:0] Byte4,
  output [7:0] Byte5,
  output [7:0] Byte6,
  output [7:0] Byte7,
  output [7:0] Byte8,
  output [7:0] Byte9
);

  wire and_1_out, and_2_out, and_3_out, and_4_out, and_5_out, and_6_out, and_7_out, and_8_out, and_9_out,
       and_10_out, and_11_out;
  wire [7:0] rom_1_data;
  wire [11:0] adder_1_out, adder_2_out, multiplexer_1_out, register_1_q;

  Register #(.width(12)) register_1 (.D(multiplexer_1_out), .clk(clk), .Q(register_1_q));  // open: en, clr
  Multiplexer #(.width(12)) multiplexer_1 (
    .in0(adder_1_out), .in1({12{1'b0}}), .out(multiplexer_1_out), .sel(and_1_out));
  and and_1 (and_1_out, ~adder_1_out[0], adder_1_out[1], ~adder_1_out[2], adder_1_out[3]);  // AND_Gate
  ROM #(.addrWidth(12)) rom_1 (.addr(adder_2_out), .data(rom_1_data));
  Adder #(.width(12)) adder_1 (.a(register_1_q), .b(12'h1), .out(adder_1_out));  // open: cin, cout
  Adder #(.width(12)) adder_2 (.a(PC), .b(register_1_q), .out(adder_2_out));  // open: cin, cout
  Register register_2 (.D(rom_1_data), .en(and_2_out), .clk(clk), .Q(Byte0));  // open: clr
  and and_2 (and_2_out, ~register_1_q[0], ~register_1_q[1], ~register_1_q[2], ~register_1_q[3]);  // AND_Gate
  Register register_3 (.D(rom_1_data), .en(and_3_out), .clk(clk), .Q(Byte1));  // open: clr
  and and_3 (and_3_out, register_1_q[0], ~register_1_q[1], ~register_1_q[2], ~register_1_q[3]);  // AND_Gate
  Register register_4 (.D(rom_1_data), .en(and_4_out), .clk(clk), .Q(Byte2));  // open: clr
  and and_4 (and_4_out, ~register_1_q[0], register_1_q[1], ~register_1_q[2], ~register_1_q[3]);  // AND_Gate
  Register register_5 (.D(rom_1_data), .en(and_5_out), .clk(clk), .Q(Byte3));  // open: clr
  and and_5 (and_5_out, register_1_q[0], register_1_q[1], ~register_1_q[2], ~register_1_q[3]);  // AND_Gate
  Register register_6 (.D(rom_1_data), .en(and_6_out), .clk(clk), .Q(Byte4));  // open: clr
  and and_6 (and_6_out, ~register_1_q[0], ~register_1_q[1], register_1_q[2], ~register_1_q[3]);  // AND_Gate
  Register register_7 (.D(rom_1_data), .en(and_7_out), .clk(clk), .Q(Byte5));  // open: clr
  and and_7 (and_7_out, register_1_q[0], ~register_1_q[1], register_1_q[2], ~register_1_q[3]);  // AND_Gate
  Register register_8 (.D(rom_1_data), .en(and_8_out), .clk(clk), .Q(Byte6));  // open: clr
  and and_8 (and_8_out, ~register_1_q[0], register_1_q[1], register_1_q[2], ~register_1_q[3]);  // AND_Gate
  Register register_9 (.D(rom_1_data), .en(and_9_out), .clk(clk), .Q(Byte7));  // open: clr
  and and_9 (and_9_out, register_1_q[0], register_1_q[1], register_1_q[2], ~register_1_q[3]);  // AND_Gate
  Register register_10 (.D(rom_1_data), .en(and_10_out), .clk(clk), .Q(Byte8));  // open: clr
  and and_10 (and_10_out, ~register_1_q[0], ~register_1_q[1], ~register_1_q[2], register_1_q[3]);  // AND_Gate
  Register register_11 (.D(rom_1_data), .en(and_11_out), .clk(clk), .Q(Byte9));  // open: clr
  and and_11 (and_11_out, register_1_q[0], ~register_1_q[1], ~register_1_q[2], register_1_q[3]);  // AND_Gate

  // Notes on the sheet:
  //   contents of rom_1 (hex, n*v repeats v):
  //   30 1 12 34 56 78 9a bc de f0
  //   Make incrementer so each clock adds one to lower c, loops back every 10 clock cycle
  //   This will almost definitely be replaced later
endmodule

module Fetch (
  input  [11:0] PC,
  input  clock,
  output [3:0] icode,
  output [3:0] ifun,
  output [3:0] rA,
  output [3:0] rB,
  output [63:0] valC
);

  wire and_1_out, and_2_out, and_3_out, or_1_out;
  wire [7:0] instructionmemory_1_byte2, instructionmemory_1_byte3, instructionmemory_1_byte4,
       instructionmemory_1_byte5, instructionmemory_1_byte6, instructionmemory_1_byte7,
       instructionmemory_1_byte8, instructionmemory_1_byte9;

  instructionMemory instructionmemory_1 (
    .PC(PC), .clk(clock), .Byte0({icode, ifun}), .Byte1({rA, rB}), .Byte2(instructionmemory_1_byte2),
    .Byte3(instructionmemory_1_byte3), .Byte4(instructionmemory_1_byte4), .Byte5(instructionmemory_1_byte5),
    .Byte6(instructionmemory_1_byte6), .Byte7(instructionmemory_1_byte7), .Byte8(instructionmemory_1_byte8),
    .Byte9(instructionmemory_1_byte9));
  and and_1 (and_1_out, icode[0], icode[1], ~icode[2], ~icode[3]);  // AND_Gate
  and and_2 (and_2_out, ~icode[0], ~icode[1], icode[2], ~icode[3]);  // AND_Gate
  and and_3 (and_3_out, icode[0], ~icode[1], icode[2], ~icode[3]);  // AND_Gate
  or or_1 (or_1_out, and_1_out, and_2_out, and_3_out);
  Multiplexer #(.width(64)) multiplexer_1 (
    .in0({instructionmemory_1_byte8, instructionmemory_1_byte7, instructionmemory_1_byte6, instructionmemory_1_byte5, instructionmemory_1_byte4, instructionmemory_1_byte3, instructionmemory_1_byte2, rA, rB}),
    .in1({instructionmemory_1_byte9, instructionmemory_1_byte8, instructionmemory_1_byte7, instructionmemory_1_byte6, instructionmemory_1_byte5, instructionmemory_1_byte4, instructionmemory_1_byte3, instructionmemory_1_byte2}),
    .out({valC[7:0], valC[15:8], valC[23:16], valC[31:24], valC[39:32], valC[47:40], valC[55:48], valC[63:56]}),
    .sel(or_1_out));

  // Notes on the sheet:
  //   logic for valC alignment, based on icode
endmodule

module System_Registers (
  input  [3:0] rB,
  input  [3:0] rA,
  input  write_enable,
  input  [3:0] register_being_written_to,
  input  [63:0] W_val,
  input  Clk,
  output [63:0] Val_A,
  output [63:0] Val_B
);

  wire [15:0] decoder_1_out0, multiplexer_1_out;
  wire [63:0] demultiplexer_1_out0, demultiplexer_1_out1, demultiplexer_1_out2, demultiplexer_1_out3,
       demultiplexer_1_out4, demultiplexer_1_out5, demultiplexer_1_out6, demultiplexer_1_out7,
       demultiplexer_1_out8, demultiplexer_1_out9, demultiplexer_1_out10, demultiplexer_1_out11,
       demultiplexer_1_out12, demultiplexer_1_out13, demultiplexer_1_out14, demultiplexer_1_out15, r0_q,
       r1_q, r2_q, r3_q, r5_q, r6_q, r7_q, r8_q, r9_q, r10_q, r11_q, r12_q, r13_q, r14_q, r15_q, rsp_4_q;

  Decoder #(.enable("false"), .select(4)) decoder_1 (
    .out0(decoder_1_out0[0]), .out1(decoder_1_out0[1]), .out2(decoder_1_out0[2]), .out3(decoder_1_out0[3]),
    .out4(decoder_1_out0[4]), .out5(decoder_1_out0[5]), .out6(decoder_1_out0[6]), .out7(decoder_1_out0[7]),
    .out8(decoder_1_out0[8]), .out9(decoder_1_out0[9]), .out10(decoder_1_out0[10]),
    .out11(decoder_1_out0[11]), .out12(decoder_1_out0[12]), .out13(decoder_1_out0[13]),
    .out14(decoder_1_out0[14]), .out15(decoder_1_out0[15]), .sel(register_being_written_to));
  Multiplexer #(.width(16)) multiplexer_1 (
    .in0({16{1'b0}}), .in1(decoder_1_out0), .out(multiplexer_1_out), .sel(write_enable));
  Demultiplexer #(.select(4), .width(64)) demultiplexer_1 (
    .out0(demultiplexer_1_out0), .out1(demultiplexer_1_out1), .out2(demultiplexer_1_out2),
    .out3(demultiplexer_1_out3), .out4(demultiplexer_1_out4), .out5(demultiplexer_1_out5),
    .out6(demultiplexer_1_out6), .out7(demultiplexer_1_out7), .out8(demultiplexer_1_out8),
    .out9(demultiplexer_1_out9), .out10(demultiplexer_1_out10), .out11(demultiplexer_1_out11),
    .out12(demultiplexer_1_out12), .out13(demultiplexer_1_out13), .out14(demultiplexer_1_out14),
    .out15(demultiplexer_1_out15), .in(W_val), .sel(register_being_written_to));
  Register #(.width(64)) r0 (.D(demultiplexer_1_out0), .en(multiplexer_1_out[0]), .clk(Clk), .Q(r0_q));  // open: clr
  Register #(.width(64)) rsp_4 (
    .D(demultiplexer_1_out4), .en(multiplexer_1_out[4]), .clk(Clk), .Q(rsp_4_q));  // open: clr
  Register #(.width(64)) r12 (
    .D(demultiplexer_1_out12), .en(multiplexer_1_out[12]), .clk(Clk), .Q(r12_q));  // open: clr
  Register #(.width(64)) r8 (.D(demultiplexer_1_out8), .en(multiplexer_1_out[8]), .clk(Clk), .Q(r8_q));  // open: clr
  Register #(.width(64)) r1 (.D(demultiplexer_1_out1), .en(multiplexer_1_out[1]), .clk(Clk), .Q(r1_q));  // open: clr
  Register #(.width(64)) r5 (.D(demultiplexer_1_out5), .en(multiplexer_1_out[5]), .clk(Clk), .Q(r5_q));  // open: clr
  Register #(.width(64)) r9 (.D(demultiplexer_1_out9), .en(multiplexer_1_out[9]), .clk(Clk), .Q(r9_q));  // open: clr
  Register #(.width(64)) r13 (
    .D(demultiplexer_1_out13), .en(multiplexer_1_out[13]), .clk(Clk), .Q(r13_q));  // open: clr
  Register #(.width(64)) r2 (.D(demultiplexer_1_out2), .en(multiplexer_1_out[2]), .clk(Clk), .Q(r2_q));  // open: clr
  Register #(.width(64)) r6 (.D(demultiplexer_1_out6), .en(multiplexer_1_out[6]), .clk(Clk), .Q(r6_q));  // open: clr
  Register #(.width(64)) r10 (
    .D(demultiplexer_1_out10), .en(multiplexer_1_out[10]), .clk(Clk), .Q(r10_q));  // open: clr
  Register #(.width(64)) r14 (
    .D(demultiplexer_1_out14), .en(multiplexer_1_out[14]), .clk(Clk), .Q(r14_q));  // open: clr
  Register #(.width(64)) r3 (.D(demultiplexer_1_out3), .en(multiplexer_1_out[3]), .clk(Clk), .Q(r3_q));  // open: clr
  Register #(.width(64)) r7 (.D(demultiplexer_1_out7), .en(multiplexer_1_out[7]), .clk(Clk), .Q(r7_q));  // open: clr
  Register #(.width(64)) r11 (
    .D(demultiplexer_1_out11), .en(multiplexer_1_out[11]), .clk(Clk), .Q(r11_q));  // open: clr
  Register #(.width(64)) r15 (
    .D(demultiplexer_1_out15), .en(multiplexer_1_out[15]), .clk(Clk), .Q(r15_q));  // open: clr
  Multiplexer #(.select(4), .width(64)) multiplexer_2 (
    .in0(r0_q), .in1(r1_q), .in2(r2_q), .in3(r3_q), .in4(rsp_4_q), .in5(r5_q), .in6(r6_q), .in7(r7_q),
    .in8(r8_q), .in9(r9_q), .in10(r10_q), .in11(r11_q), .in12(r12_q), .in13(r13_q), .in14(r14_q),
    .in15(r15_q), .out(Val_A), .sel(rA));
  Multiplexer #(.select(4), .width(64)) multiplexer_3 (
    .in0(r0_q), .in1(r1_q), .in2(r2_q), .in3(r3_q), .in4(rsp_4_q), .in5(r5_q), .in6(r6_q), .in7(r7_q),
    .in8(r8_q), .in9(r9_q), .in10(r10_q), .in11(r11_q), .in12(r12_q), .in13(r13_q), .in14(r14_q),
    .in15(r15_q), .out(Val_B), .sel(rB));
endmodule

module Decode (
  input  [7:0] clock_ctr,
  input  [3:0] icode,
  input  [63:0] valE,
  input  [63:0] valM,
  input  [3:0] rA,
  input  [3:0] rB,
  input  Clk,
  output [63:0] valA,
  output [63:0] valB
);

  wire write_logic_1_we;
  wire [3:0] write_logic_1_w_reg;
  wire [63:0] write_logic_1_w_val;

  write_logic write_logic_1 (
    .clock_ctr(clock_ctr), .icode(icode), .valE(valE), .valM(valM), .rA(rA), .rB(rB), .WE(write_logic_1_we),
    .W_val(write_logic_1_w_val), .W_reg(write_logic_1_w_reg));
  System_Registers system_registers_1 (
    .rB(rB), .rA(rA), .write_enable(write_logic_1_we), .register_being_written_to(write_logic_1_w_reg),
    .W_val(write_logic_1_w_val), .Clk(Clk), .Val_A(valA), .Val_B(valB));
endmodule

module write_logic (
  input  [7:0] clock_ctr,
  input  [3:0] icode,
  input  [63:0] valE,
  input  [63:0] valM,
  input  [3:0] rA,
  input  [3:0] rB,
  output WE,
  output [63:0] W_val,
  output [3:0] W_reg
);

  wire and_1_out, and_2_out, and_3_out, and_4_out, decoder_1_out10, decoder_1_out11, decoder_2_out2,
       decoder_2_out3, decoder_2_out6, decoder_2_out10, decoder_2_out11, decoder_3_out10, decoder_3_out11,
       or_1_out, or_2_out, or_3_out;
  wire [63:0] multiplexer_2_out, multiplexer_3_out;

  Decoder #(.enable("false"), .select(4)) decoder_1 (
    .out10(decoder_1_out10), .out11(decoder_1_out11), .sel(icode));  // open: out0, out1, out2, out3, out4, out5, out6, out7, out8, out9, out12, out13, out14, out15
  Multiplexer #(.width(4)) multiplexer_1 (.in0(rB), .in1(4'b0100), .out(W_reg), .sel(or_1_out));
  or or_1 (or_1_out, decoder_1_out10, decoder_1_out11);
  and and_1 (and_1_out, clock_ctr[0], ~clock_ctr[1], clock_ctr[2], clock_ctr[3], ~clock_ctr[4], ~clock_ctr[5], ~clock_ctr[6], ~clock_ctr[7]);  // AND_Gate
  Decoder #(.enable("false"), .select(4)) decoder_2 (
    .out2(decoder_2_out2), .out3(decoder_2_out3), .out6(decoder_2_out6), .out10(decoder_2_out10),
    .out11(decoder_2_out11), .sel(icode));  // open: out0, out1, out4, out5, out7, out8, out9, out12, out13, out14, out15
  or or_2 (or_2_out, decoder_2_out2, decoder_2_out3, decoder_2_out6, decoder_2_out10, decoder_2_out11);
  Decoder #(.enable("false"), .select(4)) decoder_3 (
    .out10(decoder_3_out10), .out11(decoder_3_out11), .sel(icode));  // open: out0, out1, out2, out3, out4, out5, out6, out7, out8, out9, out12, out13, out14, out15
  and and_2 (and_2_out, clock_ctr[0], clock_ctr[1], clock_ctr[2], clock_ctr[3], clock_ctr[4], clock_ctr[5], clock_ctr[6], clock_ctr[7]);
  and and_3 (and_3_out, and_1_out, or_2_out);
  or or_3 (or_3_out, decoder_3_out10, decoder_3_out11);
  and and_4 (and_4_out, and_2_out, or_3_out);
  Multiplexer #(.width(64)) multiplexer_2 (.in0({64{1'b0}}), .in1(valM), .out(multiplexer_2_out), .sel(and_4_out));
  Multiplexer #(.width(64)) multiplexer_3 (.in0({64{1'b0}}), .in1(valE), .out(multiplexer_3_out), .sel(and_3_out));
  assign W_val = multiplexer_3_out | multiplexer_2_out;  // OR_Gate or_4, 64 bits wide
  or or_5 (WE, and_3_out, and_4_out);

  // Notes on the sheet:
  //   %rsp
  //   we don't actually have to write to rA
  //   since we arent doing call or return
  //   ValE logic
  //   replace me
  //   with what time execustion is complete
  //   replace me
  //   ValM logic
  //   rr, ir, op, push, pop
  //   with what time memory is complete
  //   mr, pop
endmodule

module ALU (
  input  [3:0] icode,
  input  [63:0] valC,
  input  [63:0] valA,
  input  [63:0] valB,
  input  [3:0] ifun,
  output [63:0] out_6,
  output [63:0] valE
);

  wire decoder_1_out2, decoder_1_out3, decoder_1_out4, decoder_1_out5, decoder_1_out6, decoder_1_out10,
       decoder_1_out11, decoder_2_out2, decoder_2_out3, not_1_out, or_1_out, or_2_out, priority_encoder_1_p5,
       priority_encoder_2_out;
  wire [1:0] priority_encoder_1_p3;
  wire [63:0] adder_1_out, adder_2_out, and_1_out, multiplexer_1_out, multiplexer_2_out, not_2_out, xor_1_out;

  Decoder #(.select(4)) decoder_1 (
    .out2(decoder_1_out2), .out3(decoder_1_out3), .out4(decoder_1_out4), .out5(decoder_1_out5),
    .out6(decoder_1_out6), .out10(decoder_1_out10), .out11(decoder_1_out11), .sel(icode));  // open: out0, out1, out7, out8, out9, out12, out13, out14, out15, en
  Decoder #(.select(4)) decoder_2 (
    .out2(decoder_2_out2), .out3(decoder_2_out3), .sel(icode));  // open: out0, out1, out4, out5, out6, out7, out8, out9, out10, out11, out12, out13, out14, out15, en
  or or_1 (or_1_out, decoder_1_out3, decoder_1_out4, decoder_1_out5);
  // Priority_Encoder #(.select(2)) priority_encoder_1: pin names not known; wires that end beside it: decoder_1_out10, decoder_1_out11, priority_encoder_1_p3, or_1_out, priority_encoder_1_p5
  Multiplexer #(.select(2), .width(64)) multiplexer_1 (
    .in0(64'hfffffffffffffff8), .in1(64'h8), .in2(valC), .in3(valA), .out(multiplexer_1_out),
    .sel(priority_encoder_1_p3));
  Multiplexer #(.width(64)) multiplexer_2 (
    .in0({64{1'b0}}), .in1(valB), .out(multiplexer_2_out), .sel(priority_encoder_2_out));
  Priority_Encoder #(.select(1)) priority_encoder_2 (.in0(or_2_out), .in1(not_1_out), .out(priority_encoder_2_out));
  or or_2 (or_2_out, decoder_2_out2, decoder_2_out3);
  not not_1 (not_1_out, or_2_out);
  or or_3 (priority_encoder_1_p5, decoder_1_out2, decoder_1_out6);
  assign not_2_out = ~valA;  // NOT_Gate not_2, 64 bits wide
  Adder #(.width(64)) adder_1 (.a(multiplexer_1_out), .b(multiplexer_2_out), .out(adder_1_out));  // open: cin, cout
  Adder #(.width(64)) adder_2 (.a(not_2_out), .b(multiplexer_2_out), .out(adder_2_out), .cin(1'b1));  // open: cout
  assign and_1_out = multiplexer_2_out & valA;  // AND_Gate and_1, 64 bits wide
  assign xor_1_out = multiplexer_2_out ^ valA;  // XOR_Gate xor_1, 64 bits wide
  Multiplexer #(.select(2), .width(64)) multiplexer_3 (
    .in0(adder_1_out), .in1(adder_2_out), .in2(and_1_out), .in3(xor_1_out), .out(valE), .sel(ifun[1:0]));

  // Notes on the sheet:
  //   -8
  //   8
  //   clock
  //   clock_ctr
  //   0:-8
  //   1:8
  //   2:valC
  //   3:valA
  //   ALU1 + ALU2
  //   valB - valA
  //   valB & valA
  //   valB XOR valA
  //   0:add
  //   1:sub
  //   2:and
  //   3:xor
  //   6:1
  //   6:2
  //   6:3
endmodule

module CC (
  input  [63:0] valE,
  output ZF,
  output SF
);

  wire [1:0] or_5_out;
  wire [3:0] or_4_out;
  wire [7:0] or_3_out;
  wire [15:0] or_2_out;
  wire [31:0] or_1_out;

  assign or_1_out = valE[31:0] | valE[63:32];  // OR_Gate or_1, 32 bits wide
  assign or_2_out = or_1_out[15:0] | or_1_out[31:16];  // OR_Gate or_2, 16 bits wide
  assign or_3_out = or_2_out[7:0] | or_2_out[15:8];  // OR_Gate or_3, 8 bits wide
  assign or_4_out = or_3_out[3:0] | or_3_out[7:4];  // OR_Gate or_4, 4 bits wide
  assign or_5_out = or_4_out[1:0] | or_4_out[3:2];  // OR_Gate or_5, 2 bits wide
  or or_6 (ZF, or_5_out[0], or_5_out[1]);

  assign SF = valE[63];
endmodule

module dataMemory (
  input  clock,
  input  WE,
  input  RE,
  input  [63:0] valE,
  input  [63:0] valA,
  output [63:0] valM,
  output [7:0] out_7
);

  wire and_1_out, and_2_out, and_3_out, and_4_out, and_5_out, and_6_out, and_7_out, and_8_out, and_9_out,
       not_1_out, or_1_out;
  wire [3:0] adder_2_out, adder_2_out_2, adder_2_out_3, adder_2_out_4, adder_2_out_5, adder_2_out_6,
       adder_2_out_7, adder_2_out_8, adder_2_out_9, adder_2_out_10, adder_2_out_11, adder_2_out_12,
       adder_2_out_13, adder_2_out_14, adder_2_out_15, adder_2_out_16, register_1_q, register_1_q_2,
       register_1_q_3, register_1_q_4, register_1_q_5, register_1_q_6, register_1_q_7, register_1_q_8,
       register_1_q_9, register_1_q_10, register_1_q_11, register_1_q_12, register_1_q_13, register_1_q_14,
       register_1_q_15, register_1_q_16;
  wire [7:0] B0_q, B1_q, B2_q, B3_q, B4_q, B5_q, B6_q, B7_q, ram_1_dout;
  wire [63:0] adder_1_out, multiplexer_1_out, multiplexer_3_out;

  Multiplexer #(.width(64)) multiplexer_1 (.in0(valE), .in1(valA), .out(multiplexer_1_out), .sel(RE));
  Multiplexer #(.select(3), .width(8)) multiplexer_2 (
    .in0(valA[7:0]), .in1(valA[15:8]), .in2(valA[23:16]), .in3(valA[31:24]), .in4(valA[39:32]),
    .in5(valA[47:40]), .in6(valA[55:48]), .in7(valA[63:56]), .out(out_7), .sel(register_1_q[2:0]));
  Adder #(.width(64)) adder_1 (
    .a(multiplexer_1_out),
    .b({register_1_q_16, register_1_q_15, register_1_q_14, register_1_q_13, register_1_q_12, register_1_q_11, register_1_q_10, register_1_q_9, register_1_q_8, register_1_q_7, register_1_q_6, register_1_q_5, register_1_q_4, register_1_q_3, register_1_q_2, register_1_q}),
    .out(adder_1_out));  // open: cin, cout
  or or_1 (or_1_out, RE, WE);
  RAM #(.addrWidth(12)) ram_1 (.addr(adder_1_out[11:0]), .we(WE), .oe(RE), .clk(clock), .din(out_7), .dout(ram_1_dout));
  Register #(.width(64)) register_1 (
    .D(multiplexer_3_out), .en(or_1_out), .clk(clock),
    .Q({register_1_q_16, register_1_q_15, register_1_q_14, register_1_q_13, register_1_q_12, register_1_q_11, register_1_q_10, register_1_q_9, register_1_q_8, register_1_q_7, register_1_q_6, register_1_q_5, register_1_q_4, register_1_q_3, register_1_q_2, register_1_q}),
    .clr(not_1_out));
  not not_1 (not_1_out, or_1_out);
  Multiplexer #(.width(64)) multiplexer_3 (
    .in0({adder_2_out_16, adder_2_out_15, adder_2_out_14, adder_2_out_13, adder_2_out_12, adder_2_out_11, adder_2_out_10, adder_2_out_9, adder_2_out_8, adder_2_out_7, adder_2_out_6, adder_2_out_5, adder_2_out_4, adder_2_out_3, adder_2_out_2, adder_2_out}),
    .in1({64{1'b0}}), .out(multiplexer_3_out), .sel(and_1_out));
  and and_1 (and_1_out, ~adder_2_out[0], ~adder_2_out[1], ~adder_2_out[2], adder_2_out[3]);  // AND_Gate
  Adder #(.width(64)) adder_2 (
    .a({register_1_q_16, register_1_q_15, register_1_q_14, register_1_q_13, register_1_q_12, register_1_q_11, register_1_q_10, register_1_q_9, register_1_q_8, register_1_q_7, register_1_q_6, register_1_q_5, register_1_q_4, register_1_q_3, register_1_q_2, register_1_q}),
    .b(64'h1),
    .out({adder_2_out_16, adder_2_out_15, adder_2_out_14, adder_2_out_13, adder_2_out_12, adder_2_out_11, adder_2_out_10, adder_2_out_9, adder_2_out_8, adder_2_out_7, adder_2_out_6, adder_2_out_5, adder_2_out_4, adder_2_out_3, adder_2_out_2, adder_2_out}));  // open: cin, cout
  and and_2 (and_2_out, ~register_1_q[0], ~register_1_q[1], ~register_1_q[2], ~register_1_q[3]);  // AND_Gate
  and and_3 (and_3_out, register_1_q[0], ~register_1_q[1], ~register_1_q[2], ~register_1_q[3]);  // AND_Gate
  and and_4 (and_4_out, ~register_1_q[0], register_1_q[1], ~register_1_q[2], ~register_1_q[3]);  // AND_Gate
  and and_5 (and_5_out, register_1_q[0], register_1_q[1], ~register_1_q[2], ~register_1_q[3]);  // AND_Gate
  and and_6 (and_6_out, ~register_1_q[0], ~register_1_q[1], register_1_q[2], ~register_1_q[3]);  // AND_Gate
  and and_7 (and_7_out, register_1_q[0], ~register_1_q[1], register_1_q[2], ~register_1_q[3]);  // AND_Gate
  and and_8 (and_8_out, ~register_1_q[0], register_1_q[1], register_1_q[2], ~register_1_q[3]);  // AND_Gate
  and and_9 (and_9_out, register_1_q[0], register_1_q[1], register_1_q[2], ~register_1_q[3]);  // AND_Gate
  Register B0 (.D(ram_1_dout), .en(and_2_out), .clk(clock), .Q(B0_q));  // open: clr
  Register B1 (.D(ram_1_dout), .en(and_3_out), .clk(clock), .Q(B1_q));  // open: clr
  Register B2 (.D(ram_1_dout), .en(and_4_out), .clk(clock), .Q(B2_q));  // open: clr
  Register B3 (.D(ram_1_dout), .en(and_5_out), .clk(clock), .Q(B3_q));  // open: clr
  Register B4 (.D(ram_1_dout), .en(and_6_out), .clk(clock), .Q(B4_q));  // open: clr
  Register B5 (.D(ram_1_dout), .en(and_7_out), .clk(clock), .Q(B5_q));  // open: clr
  Register B6 (.D(ram_1_dout), .en(and_8_out), .clk(clock), .Q(B6_q));  // open: clr
  Register B7 (.D(ram_1_dout), .en(and_9_out), .clk(clock), .Q(B7_q));  // open: clr
  Register #(.width(64)) register_2 (
    .D({B7_q, B6_q, B5_q, B4_q, B3_q, B2_q, B1_q, B0_q}), .en(RE), .clk(clock), .Q(valM));  // open: clr

  // Notes on the sheet:
  //   read takes 10 clock cycles
endmodule

module memRWCntr (
  input  [3:0] icode,
  input  [7:0] clk_counter,
  output WE,
  output RE
);

  wire and_1_out, and_2_out, comparator_1_eq, comparator_2_eq, comparator_3_gt, comparator_4_lt,
       comparator_5_eq, comparator_6_eq, comparator_7_gt, comparator_8_lt, or_1_out, or_2_out;

  Comparator #(.width(4)) comparator_1 (.a(icode), .b(4'b0100), .eq(comparator_1_eq));  // open: gt, lt
  Comparator #(.width(4)) comparator_2 (.a(icode), .b(4'b1010), .eq(comparator_2_eq));  // open: gt, lt
  Comparator comparator_3 (.a(clk_counter), .b({8{1'b1}}), .gt(comparator_3_gt));  // open: eq, lt
  Comparator comparator_4 (.a(clk_counter), .b({8{1'b1}}), .lt(comparator_4_lt));  // open: gt, eq
  Comparator #(.width(4)) comparator_5 (.a(icode), .b(4'b0101), .eq(comparator_5_eq));  // open: gt, lt
  Comparator #(.width(4)) comparator_6 (.a(icode), .b(4'b1011), .eq(comparator_6_eq));  // open: gt, lt
  Comparator comparator_7 (.a(clk_counter), .b({8{1'b1}}), .gt(comparator_7_gt));  // open: eq, lt
  Comparator comparator_8 (.a(clk_counter), .b({8{1'b1}}), .lt(comparator_8_lt));  // open: gt, eq
  or or_1 (or_1_out, comparator_1_eq, comparator_2_eq);
  and and_1 (and_1_out, comparator_3_gt, comparator_4_lt);
  or or_2 (or_2_out, comparator_5_eq, comparator_6_eq);
  and and_2 (and_2_out, comparator_7_gt, comparator_8_lt);
  and and_3 (WE, or_1_out, and_1_out);
  and and_4 (RE, or_2_out, and_2_out);

  // Notes on the sheet:
  //   SET CORRECT TIMING
endmodule

module New_PC (
  input  [11:0] Val_P,
  input  [63:0] Val_M,
  input  [63:0] Val_C,
  input  [1:0] CC_flags,
  input  [3:0] icode,
  input  [3:0] ifun,
  input  Reset,
  output [11:0] PC_NEW
);

  wire and_1_out, and_2_out, and_3_out, and_4_out, and_5_out, and_6_out, and_7_out, and_8_out, and_9_out,
       and_10_out, and_11_out, and_12_out, and_13_out, and_14_out, and_15_out, and_16_out, and_17_out,
       and_18_out, and_19_out, and_20_out, comparator_1_eq, comparator_2_eq, comparator_3_eq,
       comparator_4_eq, comparator_5_eq, comparator_6_eq, comparator_7_eq, comparator_8_eq, comparator_9_eq,
       or_1_out, or_2_out;
  wire [2:0] controlled_buffer_3_out;

  Comparator #(.width(4)) comparator_1 (.a(icode), .b(4'b1000), .eq(comparator_1_eq));  // open: gt, lt
  Comparator #(.width(4)) comparator_2 (.a(icode), .b(4'b0111), .eq(comparator_2_eq));  // open: gt, lt
  Comparator #(.width(4)) comparator_3 (.a(ifun), .b(4'b0000), .eq(comparator_3_eq));  // open: gt, lt
  Comparator #(.width(4)) comparator_4 (.a(ifun), .b(4'b0011), .eq(comparator_4_eq));  // open: gt, lt
  Comparator #(.width(4)) comparator_5 (.a(ifun), .b(4'b0100), .eq(comparator_5_eq));  // open: gt, lt
  Comparator #(.width(4)) comparator_6 (.a(ifun), .b(4'b0010), .eq(comparator_6_eq));  // open: gt, lt
  Comparator #(.width(4)) comparator_7 (.a(ifun), .b(4'b0001), .eq(comparator_7_eq));  // open: gt, lt
  Comparator #(.width(4)) comparator_8 (.a(ifun), .b(4'b0101), .eq(comparator_8_eq));  // open: gt, lt
  Comparator #(.width(4)) comparator_9 (.a(ifun), .b(4'b0110), .eq(comparator_9_eq));  // open: gt, lt
  assign controlled_buffer_3_out[1] = comparator_1_eq ? 1'b1 : 1'bz;  // Controlled_Buffer controlled_buffer_1
  assign controlled_buffer_3_out[2] = comparator_1_eq ? 1'b0 : 1'bz;  // Controlled_Buffer controlled_buffer_2
  and and_1 (and_1_out, comparator_4_eq, CC_flags[0]);
  and and_2 (and_2_out, comparator_5_eq, ~CC_flags[0]);  // AND_Gate
  and and_3 (and_3_out, comparator_6_eq, ~CC_flags[0]);  // AND_Gate
  and and_4 (and_4_out, comparator_7_eq, CC_flags[0]);
  and and_5 (and_5_out, CC_flags[1], comparator_7_eq);
  and and_6 (and_6_out, comparator_8_eq, CC_flags[0]);
  and and_7 (and_7_out, ~CC_flags[1], comparator_8_eq);  // AND_Gate
  and and_8 (and_8_out, comparator_9_eq, ~CC_flags[0]);  // AND_Gate
  assign controlled_buffer_3_out[0] = comparator_1_eq ? 1'b0 : 1'bz;  // Controlled_Buffer controlled_buffer_3
  and and_9 (and_9_out, comparator_2_eq, comparator_3_eq);
  assign controlled_buffer_3_out[2] = and_9_out ? 1'b0 : 1'bz;  // Controlled_Buffer controlled_buffer_4
  and and_10 (and_10_out, comparator_2_eq, and_11_out);
  and and_11 (and_11_out, and_1_out, ~CC_flags[1]);  // AND_Gate
  assign controlled_buffer_3_out[2] = and_10_out ? 1'b0 : 1'bz;  // Controlled_Buffer controlled_buffer_5
  and and_12 (and_12_out, comparator_2_eq, and_2_out);
  assign controlled_buffer_3_out[2] = and_12_out ? 1'b0 : 1'bz;  // Controlled_Buffer controlled_buffer_6
  and and_13 (and_13_out, comparator_2_eq, and_14_out);
  and and_14 (and_14_out, and_3_out, CC_flags[1]);
  assign controlled_buffer_3_out[2] = and_13_out ? 1'b0 : 1'bz;  // Controlled_Buffer controlled_buffer_7
  and and_15 (and_15_out, comparator_2_eq, or_1_out);
  or or_1 (or_1_out, and_4_out, and_5_out);
  assign controlled_buffer_3_out[2] = and_15_out ? 1'b0 : 1'bz;  // Controlled_Buffer controlled_buffer_8
  and and_16 (and_16_out, comparator_2_eq, or_2_out);
  or or_2 (or_2_out, and_6_out, and_7_out);
  assign controlled_buffer_3_out[2] = and_16_out ? 1'b0 : 1'bz;  // Controlled_Buffer controlled_buffer_9
  and and_17 (and_17_out, comparator_2_eq, and_18_out);
  and and_18 (and_18_out, and_8_out, ~CC_flags[1]);  // AND_Gate
  assign controlled_buffer_3_out[2] = and_17_out ? 1'b0 : 1'bz;  // Controlled_Buffer controlled_buffer_10
  assign controlled_buffer_3_out[0] = and_9_out ? 1'b0 : 1'bz;  // Controlled_Buffer controlled_buffer_11
  assign controlled_buffer_3_out[1] = and_9_out ? 1'b1 : 1'bz;  // Controlled_Buffer controlled_buffer_12
  assign controlled_buffer_3_out[0] = and_10_out ? 1'b0 : 1'bz;  // Controlled_Buffer controlled_buffer_13
  assign controlled_buffer_3_out[1] = and_10_out ? 1'b1 : 1'bz;  // Controlled_Buffer controlled_buffer_14
  assign controlled_buffer_3_out[0] = and_12_out ? 1'b0 : 1'bz;  // Controlled_Buffer controlled_buffer_15
  assign controlled_buffer_3_out[1] = and_12_out ? 1'b1 : 1'bz;  // Controlled_Buffer controlled_buffer_16
  assign controlled_buffer_3_out[0] = and_13_out ? 1'b0 : 1'bz;  // Controlled_Buffer controlled_buffer_17
  assign controlled_buffer_3_out[1] = and_13_out ? 1'b1 : 1'bz;  // Controlled_Buffer controlled_buffer_18
  assign controlled_buffer_3_out[0] = and_15_out ? 1'b0 : 1'bz;  // Controlled_Buffer controlled_buffer_19
  assign controlled_buffer_3_out[1] = and_15_out ? 1'b1 : 1'bz;  // Controlled_Buffer controlled_buffer_20
  assign controlled_buffer_3_out[0] = and_16_out ? 1'b0 : 1'bz;  // Controlled_Buffer controlled_buffer_21
  assign controlled_buffer_3_out[1] = and_16_out ? 1'b1 : 1'bz;  // Controlled_Buffer controlled_buffer_22
  assign controlled_buffer_3_out[0] = and_17_out ? 1'b0 : 1'bz;  // Controlled_Buffer controlled_buffer_23
  assign controlled_buffer_3_out[1] = and_17_out ? 1'b1 : 1'bz;  // Controlled_Buffer controlled_buffer_24
  Multiplexer #(.select(3), .width(12)) multiplexer_1 (
    .in0(Val_P), .in1(Val_M[11:0]), .in2(Val_C[11:0]), .in3({12{1'b0}}), .out(PC_NEW),
    .sel(controlled_buffer_3_out));  // open: in4, in5, in6, in7
  and and_19 (and_19_out, ~and_9_out, ~and_10_out, ~and_12_out, ~and_13_out, ~and_15_out, ~and_16_out, ~and_17_out, ~comparator_1_eq);  // AND_Gate
  and and_20 (and_20_out, and_19_out, ~Reset);  // AND_Gate
  assign controlled_buffer_3_out[2] = and_20_out ? 1'b0 : 1'bz;  // Controlled_Buffer controlled_buffer_25
  assign controlled_buffer_3_out[1] = Reset ? 1'b1 : 1'bz;  // Controlled_Buffer controlled_buffer_26
  assign controlled_buffer_3_out[2] = Reset ? 1'b0 : 1'bz;  // Controlled_Buffer controlled_buffer_27
  assign controlled_buffer_3_out[0] = and_20_out ? 1'b0 : 1'bz;  // Controlled_Buffer controlled_buffer_28
  assign controlled_buffer_3_out[1] = and_20_out ? 1'b0 : 1'bz;  // Controlled_Buffer controlled_buffer_29
  assign controlled_buffer_3_out[0] = Reset ? 1'b1 : 1'bz;  // Controlled_Buffer controlled_buffer_30
endmodule
